# Fritzing sketch Project_scheme_v1 (saved by Fritzing 0.9.3b)
breadboards: 1

parts:
  U1 = ESP8266 WiFi Module [part_number=ESP8266]
  R1 = Resistor [tolerance=±5% resistance=10k package=THT]
  R2 = Photocell (LDR) [package=THT]
  S1 = Tilt Switch [package=THT]

nets:
  N1: U1.VCC, R2.pin_0
  N2: U1.GND, R1.Pin_1, S1.Pin_2
  N3: U1.ADC_0, R1.Pin_0, R2.pin_1
